# Fritzing sketch templogger (saved by Fritzing 0.5.2b)
breadboards: 1

parts:
  Parte1 = PINGUINO2550
  LCD1 = LCD screen
  R1 = Trimmer Potentiometer [package=THT]
  IC1 = 24LC128 [package=THT]
  S1 = Pushbutton [package="[THT]"]
  R2 = Resistor [resistance=10k package=THT]
  C1 = Ceramic Capacitor [capacitance=0.1µF rated_voltage=35V package="100 mil [THT, multilayer]"]

nets:
  N1: Parte1.connector3, LCD1.DB7
  N2: Parte1.connector4, LCD1.DB6
  N3: Parte1.connector5, LCD1.DB5
  N4: Parte1.connector6, LCD1.DB4
  N5: Parte1.connector8, S1.Pin_1, S1.Pin_2, R2.Pin_1, C1.1
  N6: Parte1.connector9, Parte1.connector10, Parte1.connector17, IC1.A0, IC1.A1, IC1.A2, IC1.0V
  N7: Parte1.connector11, LCD1.VSS, R1.leg1, IC1.+V, R2.Pin_0
  N8: Parte1.connector12, LCD1.VDD, LCD1.R/W, R1.leg2, IC1.WP_-_Write_Protect, S1.Pin_3, S1.Pin_4, C1.0
  N9: Parte1.connector13, LCD1.E
  N10: Parte1.connector14, LCD1.RS
  N11: LCD1.V0, R1.wiper
